# Fritzing sketch Drone (saved by Fritzing 0.9.3b)
breadboards: 1

parts:
  S1 = H-Bridge with L298N
  Part1 = Arduino Mega ADK (Rev3)
  Part2 = Bluetooth HC-05 Macho
  S2 = H-Bridge with L298N

nets:
  N1: S1.ENA, Part1.D7_PWM
  N2: S1.IN1, Part1.D32
  N3: S1.IN2, Part1.D33
  N4: S1.IN3, Part1.D36
  N5: S1.IN4, Part1.D37
  N6: S1.ENB, Part1.D6_PWM
  N7: Part1.D11_PWM, Part2.RXD
  N8: Part1.D10_PWM, Part2.TXD
  N9: Part1.D9_PWM, S2.ENA
  N10: Part1.D8_PWM, S2.ENB
  5V: Part1.5V, Part2.VCC
  GND: Part1.GND, Part2.GND
  N11: Part1.D24, S2.IN1
  N12: Part1.D25, S2.IN2
  N13: Part1.D28, S2.IN3
  N14: Part1.D29, S2.IN4

custom parts:
  H-Bridge with L298N: h-bridge
