# Fritzing sketch IMU (saved by Fritzing 0.9.3b)
breadboards: 1

parts:
  Part1 = Arduino Mega 2560 (Rev3)
  GY2 = MPU-6050 Board GY-521 [form="♀ (female)" package=THT]

nets:
  N1: Part1.D21/SCL, GY2.pin3
  N2: Part1.D20/SDA, GY2.pin4
  N3: Part1.5V, GY2.pin1
  N4: Part1.GND, GY2.pin2
  N5: Part1.D2_PWM, GY2.pin8

custom parts:
  MPU-6050 Board GY-521: Acelerometro y Giroscopio MPU-6050 Board GY-521
